// Logisim project Projeto_elevador_pariedade.circ as structural Verilog: 8 circuits, main circuit DISPLAY
module main (
  input  Emergencia,
  input  Motor_Habilitado,
  input  Sensor,
  input  Alinhado,
  input  B4,
  input  B3,
  input  B2,
  input  B1,
  input  B0,
  input  A4,
  input  A3,
  input  A2,
  input  A1,
  input  A0,
  input  S4,
  input  S3,
  input  S2,
  input  S1,
  input  S0,
  output Erro,
  output Erro_2,
  output Erro_3
);

  wire and_1_out, and_2_out, and_3_out, and_4_out, and_5_out, codificador_1_chamada, codificador_1_d0,
       codificador_1_d1, codificador_1_d2, codificador_2_chamada, codificador_2_d0, codificador_2_d1,
       codificador_2_d2, codificador_3_chamada, codificador_3_d0, codificador_3_d1, codificador_3_d2,
       comparador_1_descer, comparador_1_parar, comparador_1_subir, display_1_a, display_1_b, display_1_c,
       display_1_d, display_1_e, display_1_f, display_1_g, display_2_a, display_2_b, display_2_c,
       display_2_d, display_2_e, display_2_f, display_2_g, display_3_a, display_3_b, display_3_c,
       display_3_d, display_3_e, display_3_f, display_3_g, \memória_1_q0 , \memória_1_q1 , \memória_1_q2 ,
       \memória_2_q0 , \memória_2_q1 , \memória_2_q2 , \memória_3_q0 , \memória_3_q1 , \memória_3_q2 ,
       or_1_out, or_2_out, or_3_out, or_4_out, or_5_out, or_6_out, or_7_out, or_8_out, or_9_out, or_10_out,
       or_11_out, portas_1_motor_ligado, portas_1_p__aberta, portas_1_p__fechada, portas_externas_1_porta_0,
       portas_externas_1_porta_1, portas_externas_1_porta_2, portas_externas_1_porta_3,
       portas_externas_1_porta_4;

  Verificador_e_gerador_de_pariedade_par verificador_e_gerador_de_pariedade_par_1 (
    .P(Erro_3), .E4(B4), .E3(B3), .E2(B2), .E1(B1), .E0(B0));
  \Memória  \memória_1  (
    .S4(B4), .S3(B3), .S2(B2), .S1(B1), .S0(B0), .Q2(\memória_1_q2 ), .Q1(\memória_1_q1 ), .Q0(\memória_1_q0 ));
  Codificador codificador_1 (
    .D0(codificador_1_d0), .D1(codificador_1_d1), .D2(codificador_1_d2), .B4(B4), .B3(B3), .B2(B2), .B1(B1),
    .B0(B0), .Chamada(codificador_1_chamada));
  LED Chamado_Destino (.in(codificador_1_chamada));
  or or_1 (or_1_out, B4, A4);
  or or_2 (or_2_out, B3, A3);
  or or_3 (or_3_out, B1, A1);
  or or_4 (or_4_out, B2, A2);
  or or_5 (or_5_out, \memória_1_q0 , codificador_1_d0);
  or or_6 (or_6_out, \memória_1_q1 , codificador_1_d1);
  or or_7 (or_7_out, \memória_1_q2 , codificador_1_d2);
  or or_8 (or_8_out, B0, A0);
  Verificador_e_gerador_de_pariedade_par verificador_e_gerador_de_pariedade_par_2 (
    .P(Erro), .E4(A4), .E3(A3), .E2(A2), .E1(A1), .E0(A0));
  LED C__Andares (.in(codificador_2_chamada));
  DISPLAY display_1 (
    .A(display_1_a), .B(display_1_b), .C(display_1_c), .D(display_1_d), .E(display_1_e), .F(display_1_f),
    .G(display_1_g), .Bit_3(or_7_out), .Bit_2(or_6_out), .Bit_1(or_5_out));
  Codificador codificador_2 (
    .D0(codificador_2_d0), .D1(codificador_2_d1), .D2(codificador_2_d2), .B4(A4), .B3(A3), .B2(A2), .B1(A1),
    .B0(A0), .Chamada(codificador_2_chamada));
  \Memória  \memória_2  (
    .S4(A4), .S3(A3), .S2(A2), .S1(A1), .S0(A0), .Q2(\memória_2_q2 ), .Q1(\memória_2_q1 ), .Q0(\memória_2_q0 ));
  or or_9 (or_9_out, codificador_2_d2, \memória_2_q2 );
  _7_Segment_Display u_7_segment_display_1 (
    .g(display_1_g), .f(display_1_f), .a(display_1_a), .b(display_1_b), .e(display_1_e), .d(display_1_d),
    .c(display_1_c));  // open: dp
  Portas_externas portas_externas_1 (
    .Q2(codificador_3_d2), .Q1(codificador_3_d1), .Q0(codificador_3_d0), .Sinal_Abrir(portas_1_p__aberta),
    .Porta_4(portas_externas_1_porta_4), .Porta_3(portas_externas_1_porta_3),
    .Porta_2(portas_externas_1_porta_2), .Porta_1(portas_externas_1_porta_1),
    .Porta_0(portas_externas_1_porta_0));
  or or_10 (or_10_out, codificador_2_d0, \memória_2_q0 );
  or or_11 (or_11_out, codificador_2_d1, \memória_2_q1 );
  Comparador comparador_1 (
    .Parar(comparador_1_parar), .Subir(comparador_1_subir), .Descer(comparador_1_descer),
    .D2(codificador_3_d2), .D1(codificador_3_d1), .D0(codificador_3_d0), .A2(\memória_3_q2 ),
    .A1(\memória_3_q1 ), .A0(\memória_3_q0 ));
  Codificador codificador_3 (
    .D0(codificador_3_d0), .D1(codificador_3_d1), .D2(codificador_3_d2), .B4(or_1_out), .B3(or_2_out),
    .B2(or_4_out), .B1(or_3_out), .B0(or_8_out), .Chamada(codificador_3_chamada));
  LED P_E_4_Aberta (.in(portas_externas_1_porta_4));
  LED P_E_3_Aberta (.in(portas_externas_1_porta_3));
  LED P_E_2_Aberta (.in(portas_externas_1_porta_2));
  LED P_E_1_Aberta (.in(portas_externas_1_porta_1));
  LED P_E_0_Aberta (.in(portas_externas_1_porta_0));
  LED Chamado_Recebido (.in(codificador_3_chamada));
  and and_1 (and_1_out, comparador_1_subir, portas_1_p__fechada);
  and and_2 (and_2_out, and_1_out, ~Emergencia);  // AND_Gate
  and and_3 (and_3_out, comparador_1_descer, portas_1_p__fechada);
  and and_4 (and_4_out, and_3_out, ~Emergencia);  // AND_Gate
  LED LED_Subir (.in(comparador_1_subir));
  LED LED_Descer (.in(comparador_1_descer));
  LED Parado (.in(comparador_1_parar));
  and and_5 (and_5_out, comparador_1_parar, Alinhado);
  Verificador_e_gerador_de_pariedade_par verificador_e_gerador_de_pariedade_par_3 (
    .P(Erro_2), .E4(S4), .E3(S3), .E2(S2), .E1(S1), .E0(S0));
  DISPLAY display_2 (
    .A(display_2_a), .B(display_2_b), .C(display_2_c), .D(display_2_d), .E(display_2_e), .F(display_2_f),
    .G(display_2_g), .Bit_3(or_9_out), .Bit_2(or_11_out), .Bit_1(or_10_out));
  \Memória  \memória_3  (
    .S4(S4), .S3(S3), .S2(S2), .S1(S1), .S0(S0), .Q2(\memória_3_q2 ), .Q1(\memória_3_q1 ), .Q0(\memória_3_q0 ));
  DISPLAY display_3 (
    .A(display_3_a), .B(display_3_b), .C(display_3_c), .D(display_3_d), .E(display_3_e), .F(display_3_f),
    .G(display_3_g), .Bit_3(\memória_3_q2 ), .Bit_2(\memória_3_q1 ), .Bit_1(\memória_3_q0 ));
  _7_Segment_Display u_7_segment_display_2 (
    .g(display_2_g), .f(display_2_f), .a(display_2_a), .b(display_2_b), .e(display_2_e), .d(display_2_d),
    .c(display_2_c));  // open: dp
  _7_Segment_Display u_7_segment_display_3 (
    .g(display_3_g), .f(display_3_f), .a(display_3_a), .b(display_3_b), .e(display_3_e), .d(display_3_d),
    .c(display_3_c));  // open: dp
  PORTAS portas_1 (
    .E(Emergencia), .Sensor(Sensor), .Motor_Habilitado(Motor_Habilitado), .Parado_Alinhado(and_5_out),
    .Subir(and_2_out), .Descendo(and_4_out), .P__Aberta(portas_1_p__aberta),
    .P__Fechada(portas_1_p__fechada), .Motor_Ligado(portas_1_motor_ligado));
  LED Motor_Ligado (.in(portas_1_motor_ligado));
  LED P_I_Fechada (.in(portas_1_p__fechada));
  LED P_I_Aberta (.in(portas_1_p__aberta));

  // Notes on the sheet:
  //   Destino
  //   Andares
  //   Andar Atual do Elevador
endmodule

module DISPLAY (
  input  Bit_3,
  input  Bit_2,
  input  Bit_1,
  output A,
  output B,
  output C,
  output D,
  output E,
  output F,
  output G
);

  wire and_1_out, and_2_out, and_3_out, and_4_out, and_5_out;

  and and_1 (and_1_out, ~Bit_3, ~Bit_1);  // AND_Gate
  and and_2 (and_2_out, ~Bit_3, Bit_2);  // AND_Gate
  and and_3 (and_3_out, ~Bit_2, ~Bit_1);  // AND_Gate
  and and_4 (and_4_out, ~Bit_3, Bit_1);  // AND_Gate
  and and_5 (and_5_out, ~Bit_2, ~Bit_1);  // AND_Gate
  and and_6 (E, ~Bit_3, ~Bit_1);  // AND_Gate
  and and_7 (F, ~Bit_2, ~Bit_1);  // AND_Gate
  or or_1 (G, Bit_3, Bit_2);
  or or_2 (A, and_1_out, and_2_out);
  or or_3 (B, and_3_out, ~Bit_3);  // OR_Gate
  or or_4 (C, and_4_out, and_5_out);

  assign D = A;

  // Notes on the sheet:
  //   ~Bit3 ~Bit1 + ~Bit3 Bit2
  //   ~Bit2 ~Bit1 + ~Bit3
  //   ~Bit3 Bit1 + ~Bit2 ~Bit1
  //   ~Bit3 ~Bit1 + ~Bit3 Bit2
  //   ~Bit3 ~Bit1
  //   ~Bit2 ~Bit1
  //   Bit3 + Bit2
endmodule

module PORTAS (
  input  Sensor,
  input  Motor_Habilitado,
  input  Parado_Alinhado,
  input  Subir,
  input  Descendo,
  input  E,
  output Motor_Ligado,
  output P__Aberta,
  output P__Fechada
);

  wire and_1_out, and_2_out, and_3_out, and_5_out, and_6_out, and_7_out, and_8_out, clock_1_out, nor_1_out,
       or_1_out, or_2_out, or_3_out, or_4_out, t_ff_1_q, t_ff_1_qn, t_ff_2_q, t_ff_2_qn, t_ff_3_q, t_ff_3_qn,
       xor_1_out, xor_2_out;

  Clock clock_1 (.out(clock_1_out));
  and and_1 (and_1_out, t_ff_3_qn, t_ff_2_qn);
  T_Flip_Flop t_ff_1 (
    .clk(clock_1_out), .T(and_1_out), .Q(t_ff_1_q), .Qn(t_ff_1_qn), .preset(or_2_out), .en(xor_2_out));  // open: reset
  and and_2 (and_2_out, t_ff_1_q, t_ff_2_q);
  and and_3 (and_3_out, and_2_out, t_ff_3_q);
  or or_1 (or_1_out, Descendo, Subir);
  or or_2 (or_2_out, and_3_out, xor_1_out);
  xor xor_1 (xor_1_out, ~Parado_Alinhado, Sensor);  // XOR_Gate
  or or_3 (or_3_out, Motor_Habilitado, or_1_out);
  T_Flip_Flop t_ff_2 (
    .clk(clock_1_out), .T(t_ff_3_qn), .Q(t_ff_2_q), .Qn(t_ff_2_qn), .reset(or_2_out), .en(xor_2_out));  // open: preset
  or or_4 (or_4_out, or_3_out, and_6_out);
  nor nor_1 (nor_1_out, or_4_out, E);
  and and_4 (P__Aberta, Parado_Alinhado, nor_1_out);
  T_Flip_Flop t_ff_3 (
    .clk(clock_1_out), .T(Parado_Alinhado), .Q(t_ff_3_q), .Qn(t_ff_3_qn), .preset(or_2_out), .en(xor_2_out));  // open: reset
  and and_5 (and_5_out, t_ff_2_qn, t_ff_3_qn);
  and and_6 (and_6_out, t_ff_1_qn, and_5_out);
  or or_5 (P__Fechada, ~P__Aberta, or_4_out);  // OR_Gate
  xor xor_2 (xor_2_out, Parado_Alinhado, or_4_out);
  and and_7 (and_7_out, or_1_out, Motor_Habilitado);
  and and_8 (and_8_out, and_7_out, ~E);  // AND_Gate
  and and_9 (Motor_Ligado, and_8_out, ~Sensor);  // AND_Gate

  // Notes on the sheet:
  //   Expressão de Porta Aberta
  //   Sensor ~Motor Parado/Alinhado ~Subir ~Descendo ~E
  //   Expressão de Porta Fechada
  //   ~Sensor + Parado/Alinhado + E + Descendo + Subir + Motor 
  //   Expressão de Motor Habilitado
  //   ~Sensor MotorHabilitado Descendo ~E + ~Sensor MotorHabilitado Subir ~E
endmodule

module \Memória  (
  input  S4,
  input  S3,
  input  S2,
  input  S1,
  input  S0,
  output Q2,
  output Q1,
  output Q0
);

  wire or_1_out, or_2_out, or_3_out, or_4_out, or_5_out, or_6_out, or_7_out, or_8_out;

  D_Flip_Flop d_ff_1 (.Q(Q2), .preset(S4), .reset(or_1_out));  // open: clk, D, Qn, en
  or or_1 (or_1_out, or_2_out, or_5_out);
  or or_2 (or_2_out, S3, S2);
  D_Flip_Flop d_ff_2 (.Q(Q1), .preset(or_2_out), .reset(or_3_out));  // open: clk, D, Qn, en
  or or_3 (or_3_out, or_4_out, S0);
  or or_4 (or_4_out, S4, S1);
  or or_5 (or_5_out, S1, S0);
  D_Flip_Flop d_ff_3 (.Q(Q0), .preset(or_7_out), .reset(or_6_out));  // open: clk, D, Qn, en
  or or_6 (or_6_out, or_8_out, S0);
  or or_7 (or_7_out, S3, S1);
  or or_8 (or_8_out, S4, S2);

  // Notes on the sheet:
  //   Entrada do número do andar para binário
  //   Armazena o valor convertido para binário
  //   Expressões de números em binário
  //   S4 ~S3 ~S2 ~S1 ~S0 
  //   ~S4  S2 ~S1 ~S0 + ~S4 S3 ~S1 ~S0 
  //   ~S4  ~S2 S1 ~S0 + ~S4 S3 ~S2 ~S0 
endmodule

module Comparador (
  input  D2,
  input  D1,
  input  D0,
  input  A2,
  input  A1,
  input  A0,
  output Parar,
  output Subir,
  output Descer
);

  wire and_1_out, and_2_out, and_3_out, and_5_out, I0_out, I1_out, I2_out, or_1_out, V1_out, V2_out, V3_out;

  and V1 (V1_out, D2, ~A2);  // AND_Gate
  and V2 (V2_out, D1, ~A1);  // AND_Gate
  xnor I2 (I2_out, D2, A2);
  and and_1 (and_1_out, I2_out, I1_out);
  xnor I1 (I1_out, D1, A1);
  xnor I0 (I0_out, D0, A0);
  and and_2 (and_2_out, I2_out, V2_out);
  and and_3 (and_3_out, I2_out, I1_out);
  and V3 (V3_out, D0, ~A0);  // AND_Gate
  and and_4 (Parar, and_1_out, I0_out);
  or or_1 (or_1_out, V1_out, and_2_out);
  and and_5 (and_5_out, and_3_out, V3_out);
  or or_2 (Subir, or_1_out, and_5_out);
  nor nor_1 (Descer, Parar, Subir);

  // Notes on the sheet:
  //   Andares Destino
  //   Andar da Cabine
endmodule

module Codificador (
  input  B4,
  input  B3,
  input  B2,
  input  B1,
  input  B0,
  output D0,
  output D1,
  output D2,
  output Chamada
);

  wire and_1_out, and_2_out, and_3_out, and_4_out, and_5_out, and_6_out, or_3_out, or_4_out, or_6_out;

  and and_1 (and_1_out, B2, ~B4);  // AND_Gate
  and and_2 (and_2_out, B3, ~B4);  // AND_Gate
  and and_3 (and_3_out, B1, ~B2);  // AND_Gate
  and and_4 (and_4_out, and_1_out, ~B4);  // AND_Gate
  and and_5 (and_5_out, and_3_out, ~B3);  // AND_Gate
  and and_6 (and_6_out, and_5_out, ~B4);  // AND_Gate
  or or_1 (D0, and_6_out, and_2_out);
  or or_2 (D1, and_4_out, and_2_out);
  or or_3 (or_3_out, B4, or_4_out);
  or or_4 (or_4_out, B3, B2);
  or or_5 (Chamada, or_3_out, or_6_out);
  or or_6 (or_6_out, B1, B0);

  assign D2 = B4;

  // Notes on the sheet:
  //   Botão de seleção
  //   Andar do Botão em Binário
  //   B4
  //   ~B4 ~B2 B1 + ~B4 B3
  //   ~B4 B2 + ~B4 B3
  //   B0 + B1 + B2 + B3 + B4
endmodule

module Portas_externas (
  input  Q2,
  input  Q1,
  input  Q0,
  input  Sinal_Abrir,
  output Porta_4,
  output Porta_3,
  output Porta_2,
  output Porta_1,
  output Porta_0
);

  wire and_1_out, and_2_out, and_3_out, and_4_out, and_5_out, and_6_out, and_8_out, and_10_out, and_12_out,
       and_14_out;

  and and_1 (and_1_out, Q2, ~Q1);  // AND_Gate
  and and_2 (and_2_out, ~Q2, Q1);  // AND_Gate
  and and_3 (and_3_out, ~Q2, Q1);  // AND_Gate
  and and_4 (and_4_out, ~Q2, ~Q1);  // AND_Gate
  and and_5 (and_5_out, ~Q2, ~Q1);  // AND_Gate
  and and_6 (and_6_out, and_1_out, ~Q0);  // AND_Gate
  and and_7 (Porta_4, and_6_out, Sinal_Abrir);
  and and_8 (and_8_out, and_2_out, Q0);
  and and_9 (Porta_3, and_8_out, Sinal_Abrir);
  and and_10 (and_10_out, and_3_out, ~Q0);  // AND_Gate
  and and_11 (Porta_2, and_10_out, Sinal_Abrir);
  and and_12 (and_12_out, and_4_out, Q0);
  and and_13 (Porta_1, and_12_out, Sinal_Abrir);
  and and_14 (and_14_out, and_5_out, ~Q0);  // AND_Gate
  and and_15 (Porta_0, and_14_out, Sinal_Abrir);
endmodule

module Verificador_e_gerador_de_pariedade_par (
  input  E4,
  input  E3,
  input  E2,
  input  E1,
  input  E0,
  output P
);

  wire xor_1_out, xor_2_out, xor_3_out, xor_4_out, xor_5_out, xor_6_out, xor_7_out, xor_8_out;

  xor xor_1 (xor_1_out, E0, E1);
  xor xor_2 (xor_2_out, E2, E3);
  xor xor_3 (xor_3_out, E0, E1);
  xor xor_4 (xor_4_out, E2, E3);
  xor xor_5 (xor_5_out, xor_1_out, xor_2_out);
  xor xor_6 (xor_6_out, xor_3_out, xor_4_out);
  xor xor_7 (xor_7_out, xor_5_out, E4);
  xor xor_8 (xor_8_out, xor_6_out, E4);
  xor xor_9 (P, xor_7_out, xor_8_out);
endmodule
